# Fritzing sketch diplsay-oled-01-test (saved by Fritzing 0.9.4)

parts:
  0_91_Inch_I2C_OLED_Display1 = 0.91 Inch I2C OLED Display
  Componente1 = Arduino Uno (Rev3)

nets:
  GND: 0_91_Inch_I2C_OLED_Display1.GND, Componente1.GND
  VCC: 0_91_Inch_I2C_OLED_Display1.VCC, Componente1.5V
  N1: 0_91_Inch_I2C_OLED_Display1.SCK, Componente1.A5/SCL
  N2: 0_91_Inch_I2C_OLED_Display1.SDA, Componente1.A4/SDA

custom parts:
  0.91 Inch I2C OLED Display: Strong contrast by the use of the innovative OLED technology in the wide 0.91 inch Display! Due to the high resolution of 128x32 pixels the Display offers plenty of space to Display items! Easy connection of the display with Arduino, Raspberry Pi, and co. by I2C interface only four Pins! Thanks To The Standard Controller (SSD 1306) already libraries for Arduino, Raspberry Pi, and co. exist,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
