# Fritzing sketch leds-rgb-01-test (saved by Fritzing 0.9.4)
breadboards: 1

parts:
  LED1 = RGB LED (com. cathode, rgb) [package="5 mm [THT]"]
  LED2 = RGB LED - (4 legs) [package="5 mm [THT]"]
  R1 = Resistor [tolerance=±5% resistance=220 package=THT]
  R2 = Resistor [tolerance=±5% resistance=220 package=THT]
  R3 = Resistor [tolerance=±5% resistance=220 package=THT]
  R4 = Resistor [tolerance=±5% resistance=220 package=THT]
  R5 = Resistor [tolerance=±5% resistance=220 package=THT]
  R6 = Resistor [tolerance=±5% resistance=220 package=THT]
  Componente1 = Arduino Uno (Rev3)

nets:
  N1: LED1.red_anode, R2.Pin_0
  N2: LED1.common_cathode, Componente1.5V
  N3: LED1.green_anode, R3.Pin_0
  N4: LED1.blue_anode, R4.Pin_0
  N5: LED2.red_cathode, R5.Pin_0
  N6: LED2.common_anode, Componente1.GND
  N7: LED2.green_cathode, R6.Pin_0
  N8: LED2.blue_cathode, R1.Pin_0
  N9: R1.Pin_1, Componente1.A5/SCL
  N10: R2.Pin_1, Componente1.A0
  N11: R3.Pin_1, Componente1.A1
  N12: R4.Pin_1, Componente1.A2
  N13: R5.Pin_1, Componente1.A3
  N14: R6.Pin_1, Componente1.A4/SDA
