# Fritzing sketch receptor (saved by Fritzing 0.9.2b)
breadboards: 1

parts:
  R1 = Resistor [tolerance=±5% resistance=220 package=THT]
  R2 = Resistor [tolerance=±5% resistance=220 package=THT]
  LED1 = LED - 5mm [color="Red (633nm)" package="5 mm [THT]"]
  LED2 = LED - 5mm [color="Red (633nm)" package="5 mm [THT]"]
  Componente1 = Arduino Uno (Rev3)
  U1 = RF-LINK_RX [package=rf-link_rx]

nets:
  N1: R1.Pin_0, LED2.cathode
  GND: R1.Pin_1, R2.Pin_1, Componente1.GND, U1.GND
  N2: R2.Pin_0, LED1.cathode
  5V: LED1.anode, Componente1.5V, U1.VCC
  N3: LED2.anode, Componente1.D4
  N4: Componente1.D5_PWM, U1.Data

custom parts:
  RF-LINK_RX: RF Link receivers- WRL-8947, 8948, 8949, 8950
