# Fritzing sketch transmissor (saved by Fritzing 0.9.2b)
breadboards: 1

parts:
  U1 = RF-LINK_TX [package=rf-link_tx]
  R1 = Resistor [tolerance=±5% resistance=220 package=THT]
  LED1 = LED - 5mm [color="Red (633nm)" package="5 mm [THT]"]
  Componente1 = Arduino Uno (Rev3)

nets:
  N1: U1.DATA, Componente1.D8
  GND: U1.GND, R1.Pin_1, Componente1.GND
  +5V: U1.+5V, LED1.anode, Componente1.5V
  N2: R1.Pin_0, LED1.cathode

custom parts:
  RF-LINK_TX: Common RF transmitter of the 315.00Mhz varity
